# Fritzing sketch breadboard (saved by Fritzing 0.9.4)
breadboards: 1

parts:
  WeMos_D1_Mini1 = WeMos D1 Mini  # not connected
  R1 = Resistor [tolerance=±5% resistance=220 package="0603 [SMD]"]
  LED1 = LED - 3mm [color="Red (633nm)" package="3 mm [THT]"]
  S1 = Momentary Switch [package=ksa_sealed_tac_switch]
  ENCODER1 = Rotary Encoder with Knob

nets:
  N1: R1.Pin_0, LED1.anode
  N2: LED1.cathode, S1.3, ENCODER1.no_name_yet#4

custom parts:
  Rotary Encoder with Knob: Rotary Encoder with 1/4" Shaft and Knob
